# Fritzing sketch 매킨토시Sketch (saved by Fritzing 0.9.10b)

parts:
  부품1 = Adafruit QT Py ESP32-S3 [part_number=5426]
  부품2 = Adafruit 1.3in 240x240 IPS TFT [part_number="Adafruit #4313"]
  부품3 = Adafruit SDIO microSD Breakout

nets:
  N1: 부품1.A0, 부품2.RESET
  N2: 부품1.A1, 부품2.BACKLIGHT
  N3: 부품1.A2, 부품2.TFTDC
  N4: 부품1.A3, 부품3.CS
  N5: 부품1.SDA, 부품2.MISO
  N6: 부품1.SCL, 부품2.SCK
  N7: 부품1.SCK, 부품3.SCLK
  N8: 부품1.MISO, 부품2.MOSI, 부품3.DI
  N9: 부품1.MOSI, 부품3.DO
  3.3V: 부품1.3.3V, 부품2.+3V3, 부품3.3.3V
  GND: 부품1.GND, 부품2.GND, 부품3.GND

custom parts:
  Adafruit QT Py ESP32-S3: The ESP32-S3 has arrived in QT Py format - and what a great way to get started with this powerful new chip from Espressif! With dual 240 MHz cores, WiFi and BLE support, and native USB, this QT Py is great for powering your IoT projects. The ESP32-S3 is a highly-integrated, low-power, 2.4 GHz Wi-Fi System-on-Chip (SoC) solution that now has WiFi and BLE support, built-in native USB as well as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
  Adafruit 1.3in 240x240 IPS TFT: We've been looking for a display like this for a long time - it's so small only 1.3" diagonal but has a high density 260 ppi, 240x240 pixel display with full-angle viewing. It looks a lot like our 1.44" 128x128 display, but has 4x as many pixels and looks great at any angle. We've seen displays of this caliber used in smartwatches and small electronic devices but they've always been MIPI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

// code stored in the sketch: MjpegClass.h.ino
//MjpegClass.h
#ifndef _MJPEGCLASS_H_
#define _MJPEGCLASS_H_


#define READ_BUFFER_SIZE 1024
#define MAXOUTPUTSIZE 16
#define NUMBER_OF_DRAW_BUFFER 1
#define DRAWTASKMALLOC  MAXOUTPUTSIZE * 16 * 16 * 2
#define DRAWTASKCORE 1



#include <freertos/FreeRTOS.h>
#include <freertos/task.h>
#include <freertos/queue.h>


#include <esp_heap_caps.h>
#include <FS.h>


#include <JPEGDEC.h>


typedef struct
{
  JPEG_DRAW_CALLBACK *drawFunc;
} paramDrawTask;


static xQueueHandle xqh = 0;
static JPEGDRAW jpegdraws[NUMBER_OF_DRAW_BUFFER];
static int queue_cnt, draw_cnt;


static int queueDrawMCU(JPEGDRAW *pDraw)
{
  ++queue_cnt;
  while ((queue_cnt - draw_cnt) > NUMBER_OF_DRAW_BUFFER)
  {
    delay(1);
  }


  int len = pDraw->iWidth * pDraw->iHeight * 2;
  JPEGDRAW *j = &jpegdraws[queue_cnt % NUMBER_OF_DRAW_BUFFER];
  j->x = pDraw->x;
  j->y = pDraw->y;
  j->iWidth = pDraw->iWidth;
  j->iHeight = pDraw->iHeight;
  memcpy(j->pPixels, pDraw->pPixels, len);


  xQueueSend(xqh, &j, 0);
  return 1;
}


static void drawTask(void *arg)
{
  paramDrawTask *p = (paramDrawTask *)arg;
  uint16_t *drawBuffer = NULL;


  for (int i = 0; i < NUMBER_OF_DRAW_BUFFER; i++)
  {
    // ? ?? ???? ?? ??? ??
    if (drawBuffer != NULL)
    {
      free(drawBuffer);
      drawBuffer = NULL;
    }


    // ??? drawBuffer ??
    drawBuffer = (uint16_t *)heap_caps_malloc(MAXOUTPUTSIZE * 16 * 16 * 2, MALLOC_CAP_DMA);
    if (drawBuffer == NULL)
    {
      // ??? ?? ?? ??
      Serial.println(F("Failed to allocate memory for drawBuffer"));
      vTaskDelete(NULL);
    }


    // ?? ??? ??????? ??? drawBuffer? ??
    jpegdraws[i].pPixels = drawBuffer;
  }
  JPEGDRAW *pDraw;
  //Serial.println("drawTask start");
  while (xQueueReceive(xqh, &pDraw, portMAX_DELAY))
  {
    // Serial.printf("task work: x: %d, y: %d, iWidth: %d, iHeight: %d\r\n", pDraw->x, pDraw->y, pDraw->iWidth, pDraw->iHeight);
    p->drawFunc(pDraw);
    // Serial.println("task work done");
    ++draw_cnt;
  }
  if (drawBuffer != NULL)
  {
    free(drawBuffer);
    drawBuffer = NULL;
  }


  vQueueDelete(xqh);
  vTaskDelete(NULL);
}


class MjpegClass
{
public:
  bool setup(Stream *input, uint8_t *mjpeg_buf, JPEG_DRAW_CALLBACK *pfnDraw, bool enableMultiTask, bool useBigEndian)
  {
    _input = input;
    _mjpeg_buf = mjpeg_buf;
    _pfnDraw = pfnDraw;
    _enableMultiTask = enableMultiTask;
    _useBigEndian = useBigEndian;


    _mjpeg_buf_offset = 0;
    _inputindex = 0;
    _remain = 0;


    queue_cnt = 0;
    draw_cnt = 0;


    if (!_read_buf)
    {
      _read_buf = (uint8_t *)malloc(READ_BUFFER_SIZE);
    }


    if (_enableMultiTask)
    {
      if (!xqh)
      {
        TaskHandle_t task;
        _p.drawFunc = pfnDraw;
        xqh = xQueueCreate(NUMBER_OF_DRAW_BUFFER, sizeof(JPEGDRAW));
        xTaskCreatePinnedToCore(drawTask, "drawTask", DRAWTASKMALLOC, &_p, 1, &task, DRAWTASKCORE);
      }
    }


    return true;
  }


  bool readMjpegBuf()// Mjpeg ??? ??
  {
    if (_inputindex == 0)
    {
      _buf_read = _input->readBytes(_read_buf, READ_BUFFER_SIZE);
      _inputindex += _buf_read;
    }
    _mjpeg_buf_offset = 0;
    int i = 0;
    bool found_FFD8 = false;
    while ((_buf_read > 0) && (!found_FFD8))//??? ??? ?? ???
    {
      i = 0;
      while ((i < _buf_read) && (!found_FFD8))
      {
        if ((_read_buf[i] == 0xFF) && (_read_buf[i + 1] == 0xD8)) // JPEG header-->FFD8
        {
          // Serial.printf("Found FFD8 at: %d.\n", i);
          found_FFD8 = true;
        }
        ++i;
      }
      if (found_FFD8)
      {
        --i;
      }
      else
      {
        _buf_read = _input->readBytes(_read_buf, READ_BUFFER_SIZE);
      }
    }
    uint8_t *_p = _read_buf + i;
    _buf_read -= i;
    bool found_FFD9 = false;
    if (_buf_read > 0)
    {
      i = 3;
      while ((_buf_read > 0) && (!found_FFD9))//??? ????? ?? ??? ???
      {
        if ((_mjpeg_buf_offset > 0) && (_mjpeg_buf[_mjpeg_buf_offset - 1] == 0xFF) && (_p[0] == 0xD9)) // JPEG trailer--->FFD9
        {
          // Serial.printf("Found FFD9 at: %d.\n", i);
          found_FFD9 = true;
        }
        else
        {
          while ((i < _buf_read) && (!found_FFD9))
          {
            if ((_p[i] == 0xFF) && (_p[i + 1] == 0xD9)) // JPEG trailer
            {
              found_FFD9 = true;
              ++i;
            }
            ++i;
          }
        }


        // Serial.printf("i: %d\n", i);
        memcpy(_mjpeg_buf + _mjpeg_buf_offset, _p, i); //??? ??? ???? _P ?? ???? ??
        _mjpeg_buf_offset += i;
        size_t o = _buf_read - i;
        if (o > 0)
        {
          // Serial.printf("o: %d\n", o);
          memcpy(_read_buf, _p + i, o);
          _buf_read = _input->readBytes(_read_buf + o, READ_BUFFER_SIZE - o);
          _p = _read_buf;
          _inputindex += _buf_read;
          _buf_read += o;
          // Serial.printf("_buf_read: %d\n", _buf_read);
        }
        else
        {
          _buf_read = _input->readBytes(_read_buf, READ_BUFFER_SIZE);
          _p = _read_buf;
          _inputindex += _buf_read;
        }
        i = 0;
      }
      if (found_FFD9)
      {
        return true;
      }
    }


    return false;
  }


  int getWidth()
  {
    return _jpeg.getWidth();
  }


  int getHeight()
  {
    return _jpeg.getHeight();
  }


  bool drawJpg()
  {
    _remain = _mjpeg_buf_offset;


    if (_enableMultiTask)
    {
      _jpeg.openRAM(_mjpeg_buf, _remain, queueDrawMCU);
    }
    else
    {
      _jpeg.openRAM(_mjpeg_buf, _remain, _pfnDraw);
    }


    _jpeg.setMaxOutputSize(MAXOUTPUTSIZE);
    if (_useBigEndian)
    {
      _jpeg.setPixelType(RGB565_BIG_ENDIAN);
    }
    _jpeg.decode(0, 0, 0);
    _jpeg.close();


    return true;
  }


private:
  Stream *_input;
  uint8_t *_mjpeg_buf;
  JPEG_DRAW_CALLBACK *_pfnDraw;
  bool _enableMultiTask;
  bool _useBigEndian;


  uint8_t *_read_buf;
  int32_t _mjpeg_buf_offset;


  JPEGDEC _jpeg;
  paramDrawTask _p;


  int32_t _inputindex;
  int32_t _buf_read;
  int32_t _remain;
};


#endif // _MJPEGCLASS_H_

// code stored in the sketch: SDMMC_MJPEG_JPEGDEC_MP3_audio.ino
//SDMMC_MJPEG_JPEGDEC_MP3_audio.ino



// MP3 ??? ?? ? ?? ??
#define MP3_FILENAME "/video.mp3"
// ?? ??? ??? ??
#define FPS 30
// MJPEG ??? ??? ?? ? ?? ??
#define MJPEG_FILENAME "/video.mjpeg"
// MJPEG ?? ?? ?? (??)
#define MJPEG_BUFFER_SIZE (240 * 240 * 2/4)
// displaying ??? ??? ??
#define DISPLAYINGMALLOC  57600
// displaying ??? ?? ??
#define DISPLAYINGCORE  0



// ??? ????? ??
#include <WiFi.h>          // ??? ?? ???? ?? ????? (?? ???)
#include <SD_MMC.h>        // SD ?? ?? ?????
#include <SD.h>            // SD ?? ?? ?????
#include <Arduino_GFX_Library.h> // ????? ??? ?? ?????


// SPI ??? ?? ? ??
#define SCK 7
#define MOSI 9
#define MISO 8


#define SS 4 // SD ?? CS ?


#define TFT_BRIGHTNESS 128 // ????? ?? ??
#define TFT_BL 2           // ????? ???? ?
#define TFT_DC 3           // ????? DC ?
#define TFT_CS -1          // ????? CS ? (???? ??)
#define TFT_RES 1          // ????? Reset ?
#define TFT_ROT 4          // ?? ??
#define TFT_WIDTH 240      // ????? ?? ??
#define TFT_HEIGHT 240     // ????? ?? ??


// ST7789 ????? ??
Arduino_HWSPI *bus = new Arduino_HWSPI(TFT_DC, TFT_CS, SCK, MOSI, MISO); // DC/CS/SCK/MOSI/MISO -> SPI ?? ? ??
Arduino_ST7789 *gfx = new Arduino_ST7789(bus, TFT_RES, TFT_ROT, true, TFT_WIDTH, TFT_HEIGHT, 0, 0); // ????? ??


/* MP3 ??? */
#include <AudioFileSourceFS.h>
#include <AudioFileSourceID3.h>
#include <AudioGeneratorMP3.h>
#include <AudioOutputI2S.h>
static AudioGeneratorMP3 *mp3;
static AudioOutputI2S *out;


/* MJPEG ??? */
#include "MjpegClass.h"
static MjpegClass mjpeg;
uint8_t *mjpeg_buf;


/* ??? */
static unsigned long total_play_audio, total_read_video, total_decode_video, total_show_video;
static unsigned long start_ms, curr_ms, next_frame_ms;
static int skipped_frames, next_frame, time_used, total_frames;
TaskHandle_t Task1;


// ?? ??? ??
static int drawMCU(JPEGDRAW *pDraw)
{
  unsigned long s = millis();
  gfx->draw16bitBeRGBBitmap(pDraw->x, pDraw->y, pDraw->pPixels, pDraw->iWidth, pDraw->iHeight);
  total_show_video += millis() - s;
  return 1;
} /* drawMCU() */


void setup()
{
  WiFi.mode(WIFI_OFF);
  Serial.begin(115200);


  // ??? ???
  gfx->begin();


  gfx->fillScreen(YELLOW);
  delay(2000);
  gfx->fillScreen(BLACK);
  delay(1000);


#ifdef TFT_BL
  ledcSetup(1, 12000, 8);       // 12 kHz PWM, 8-bit resolution
  ledcAttachPin(TFT_BL, 1);     // TFT_BL ?? ?? 1? ??
  ledcWrite(1, TFT_BRIGHTNESS); // ?? ?? (0 - 255)
#endif


  // SD ?? ???
  if (!SD.begin(SS, SPI, 80000000)) // SPI ?? ??? SD ?? ??? ? ?? ?? ??
  {
    Serial.println(F("ERROR: SD card mount failed!"));
    gfx->println(F("ERROR: SD card mount failed!"));
    exit(1);
  }
  Serial.println(F("SD Success!!"));


  out = new AudioOutputI2S(0, 1, 64); // ?? DAC? ?? ??
  mp3 = new AudioGeneratorMP3();


  mjpeg_buf = (uint8_t *)malloc(MJPEG_BUFFER_SIZE);
  xTaskCreatePinnedToCore(
      displaying,     // ??? ??
      "Task1",        // ??? ??
      DISPLAYINGMALLOC,          // ?? ?? (?? ??)
      NULL,           // ??? ????
      1,              // ??? ????
      &Task1,         // ??? ??
      DISPLAYINGCORE);


#ifdef TFT_BL
  delay(6000);
  ledcDetachPin(TFT_BL);
#endif
  gfx->displayOff();
}


void displaying(void *param)
{
  Serial.print(F("# Task 1 running on core "));
  Serial.println(F(xPortGetCoreID()));


  if (!mjpeg_buf)
  {
    Serial.println(F("mjpeg_buf malloc failed!"));
    gfx->println(F("mjpeg_buf malloc failed!"));
    exit(1);
  }
  AudioFileSourceFS *aFile = new AudioFileSourceFS(SD, MP3_FILENAME);
  File vFile = SD.open(MJPEG_FILENAME);
  if (!vFile || vFile.isDirectory())
  {
    Serial.println(F("ERROR: Failed to open " MJPEG_FILENAME " file for reading"));
    gfx->println(F("ERROR: Failed to open " MJPEG_FILENAME " file for reading"));
    exit(1);
  }


  Serial.println(F("PCM audio MJPEG video start"));


  // ??? ???
  mjpeg.setup(&vFile, mjpeg_buf, drawMCU, true, true);


  // ??? ???
  mp3->begin(aFile, out);


  skipped_frames = 0;
  total_play_audio = 0;
  total_read_video = 0;
  total_decode_video = 0;
  total_show_video = 0;
  next_frame = 0;
  total_frames = 0;
  start_ms = millis();
  curr_ms = start_ms;
  next_frame_ms = start_ms + (++next_frame * 1000 / FPS);


  while (vFile.available() && mjpeg.readMjpegBuf()) // ??? ??
  {
    // ??? ??? ??? ?? ?? ??
    Serial.println(configMINIMAL_STACK_SIZE);


    total_read_video += millis() - curr_ms;
    curr_ms = millis();


    if (millis() < next_frame_ms) // ??? ?? ?? ?? ??
    {
      // ??? ??
      mjpeg.drawJpg();
      total_decode_video += millis() - curr_ms;
    }
    else
    {
      ++skipped_frames;
      Serial.println(F("Skip frame"));
    }
    curr_ms = millis();


    // ??? ??
    if ((mp3->isRunning()) && (!mp3->loop()))
    {
      mp3->stop();
    }
    total_play_audio += millis() - curr_ms;


    while (millis() < next_frame_ms) //?? ??? ???? ??
    {
      vTaskDelay(1);
    }


    curr_ms = millis();
    next_frame_ms = start_ms + (++next_frame * 1000 / FPS);
  }
  time_used = millis() - start_ms;
  Serial.println(F("PCM audio MJPEG video end"));
  vFile.close();//??? ? ??? ?? ??
  aFile->close();


  display_stat();


  delay(10000);
}


void loop()
{
}


#define CHART_MARGIN 24
#define LEGEND_A_COLOR 0xE0C3
#define LEGEND_B_COLOR 0x33F7
#define LEGEND_C_COLOR 0x4D69
#define LEGEND_D_COLOR 0x9A74
#define LEGEND_E_COLOR 0xFBE0
#define LEGEND_F_COLOR 0xFFE6
#define LEGEND_G_COLOR 0xA2A5



// ?? ? ?? ?? ?? ??
void display_stat()
{
  int played_frames = total_frames - skipped_frames;
  float fps = 1000.0 * played_frames / time_used;
  Serial.printf("Played frames: %d\n", played_frames);
  Serial.printf("Skipped frames: %d (%0.1f %%)\n", skipped_frames, 100.0 * skipped_frames / total_frames);
  Serial.printf("Time used: %d ms\n", time_used);
  Serial.printf("Expected FPS: %d\n", FPS);
  Serial.printf("Actual FPS: %0.1f\n", fps);
  Serial.printf("Play MP3: %lu ms (%0.1f %%)\n", total_play_audio, 100.0 * total_play_audio / time_used);
  Serial.printf("SDMMC read MJPEG: %lu ms (%0.1f %%)\n", total_read_video, 100.0 * total_read_video / time_used);
  Serial.printf("Decode video: %lu ms (%0.1f %%)\n", total_decode_video, 100.0 * total_decode_video / time_used);
  Serial.printf("Show video: %lu ms (%0.1f %%)\n", total_show_video, 100.0 * total_show_video / time_used);


  gfx->setCursor(0, 0);
  gfx->setTextColor(WHITE);
  gfx->printf("Played frames: %d\n", played_frames);
  gfx->printf("Skipped frames: %d (%0.1f %%)\n", skipped_frames, 100.0 * skipped_frames / total_frames);
  gfx->printf("Actual FPS: %0.1f\n\n", fps);
  int16_t r1 = ((gfx->height() - CHART_MARGIN - CHART_MARGIN) / 2);
  int16_t r2 = r1 / 2;
  int16_t cx = gfx->width() - gfx->height() + CHART_MARGIN + CHART_MARGIN - 1 + r1;
  int16_t cy = r1 + CHART_MARGIN;
  float arc_start = 0;
  float arc_end = max(2.0, 360.0 * total_play_audio / time_used);
  for (int i = arc_start + 1; i < arc_end; i += 2)
  {
    gfx->fillArc(cx, cy, r1, r2, arc_start - 90.0, i - 90.0, LEGEND_D_COLOR);
  }
  gfx->fillArc(cx, cy, r1, r2, arc_start - 90.0, arc_end - 90.0, LEGEND_D_COLOR);
  gfx->setTextColor(LEGEND_D_COLOR);
  gfx->printf("Play MP3:\n%0.1f %%\n", 100.0 * total_play_audio / time_used);


  arc_start = arc_end;
  arc_end += max(2.0, 360.0 * total_read_video / time_used);
  for (int i = arc_start + 1; i < arc_end; i += 2)
  {
    gfx->fillArc(cx, cy, r1, r2, arc_start - 90.0, i - 90.0, LEGEND_C_COLOR);
  }
  gfx->fillArc(cx, cy, r1, r2, arc_start - 90.0, arc_end - 90.0, LEGEND_C_COLOR);
  gfx->setTextColor(LEGEND_C_COLOR);
  gfx->printf("Read MJPEG:\n%0.1f %%\n", 100.0 * total_read_video / time_used);


  arc_start = arc_end;
  arc_end += max(2.0, 360.0 * total_decode_video / time_used);
  for (int i = arc_start + 1; i < arc_end; i += 2)
  {
    gfx->fillArc(cx, cy, r1, r2, arc_start - 90.0, i - 90.0, LEGEND_B_COLOR);
  }
  gfx->fillArc(cx, cy, r1, r2, arc_start - 90.0, arc_end - 90.0, LEGEND_B_COLOR);
  gfx->setTextColor(LEGEND_B_COLOR);
  gfx->printf("Decode video:\n%0.1f %%\n", 100.0 * total_decode_video / time_used);


  arc_start = arc_end;
  arc_end += max(2.0, 360.0 * total_show_video / time_used);
  for (int i = arc_start + 1; i < arc_end; i += 2)
  {
    gfx->fillArc(cx, cy, r2, 0, arc_start - 90.0, i - 90.0, LEGEND_A_COLOR);
  }
  gfx->fillArc(cx, cy, r2, 0, arc_start - 90.0, arc_end - 90.0, LEGEND_A_COLOR);
  gfx->setTextColor(LEGEND_A_COLOR);
  gfx->printf("Play video:\n%0.1f %%\n", 100.0 * total_show_video / time_used);
}
